# Fritzing sketch SSPP2021 Motor Control (saved by Fritzing 0.9.4)

parts:
  Part1 = RAMPS_1-41  # not connected
  X1 = DB25 [package=db25]
  Axis_6 = Stepper Motor - Bipolar
  Axis_5 = Stepper Motor - Bipolar
  Axis_4 = Stepper Motor - Bipolar
  Axis_3 = Stepper Motor - Bipolar
  Axis_1 = Stepper Motor - Bipolar
  Axis_2 = Stepper Motor - Bipolar
  X2 = DB25 [package=db25]  # not connected

nets:
  N1: X1.1, Axis_6.D
  N2: X1.2, Axis_6.B
  N3: X1.3, Axis_6.C
  N4: X1.4, Axis_6.A
  N5: X1.5, Axis_5.D
  N6: X1.6, Axis_5.B
  N7: X1.7, Axis_5.C
  N8: X1.8, Axis_5.A
  N9: X1.9, Axis_4.D
  N10: X1.10, Axis_4.B
  N11: X1.11, Axis_4.C
  N12: X1.12, Axis_4.A
  N13: X1.14, Axis_3.D
  N14: X1.15, Axis_3.B
  N15: X1.16, Axis_3.C
  N16: X1.17, Axis_3.A
  N17: X1.18, Axis_2.D
  N18: X1.19, Axis_2.B
  N19: X1.20, Axis_2.C
  N20: X1.21, Axis_2.A
  N21: X1.22, Axis_1.D
  N22: X1.23, Axis_1.B
  N23: X1.24, Axis_1.C
  N24: X1.25, Axis_1.A
