# Fritzing sketch SSPP2021 Motor Control2 (saved by Fritzing 0.9.4)

parts:
  Part1 = RAMPS_1-41
  X2 = DB25 [package=db25]
  Axis_1_Driver = SIP - 13 pins [chip_label="TB6600 Motor Driver" package="SIP (Single Inline) [THT]"]
  VCC1 = Battery block 9V
  Axis_2_Driver = SIP - 13 pins [chip_label="TB6600 Motor Driver" package="SIP (Single Inline) [THT]"]
  Axis_3_Driver = SIP - 13 pins [chip_label="TB6600 Motor Driver" package="SIP (Single Inline) [THT]"]
  Part2 = Bluetooth HC-05 Macho
  LED1 = smd LED [color="Red (633nm)" package="0603 [SMD]"]
  R1 = Resistor [tolerance=±5% resistance=220 package="2512 [SMD]"]
  Part3 = NRF24L01+ Breakout Board

nets:
  VCC: Part1.VCC, Part2.VCC, Part3.VCC
  GND: Part1.GND, Part2.GND, LED1.cathode, Part3.GND
  N1: Part1.D2, Part2.RXD
  N2: Part1.D1, Part2.TXD
  N3: Part1.D11, R1.Pin_1
  N4: Part1.D49, Part3.CS
  N5: Part1.MISO, Part3.MISO
  N6: Part1.MOSI, Part3.MOSI
  N7: Part1.SCK, Part3.SCK
  N8: Part1.D53, Part3.CE
  N9: Part1.D47, Axis_3_Driver.PUL+
  N10: Part1.D45, Axis_3_Driver.DIR+
  N11: Part1.D43, Axis_2_Driver.PUL+
  N12: Part1.D41, Axis_2_Driver.DIR+
  N13: Part1.D39, Axis_1_Driver.PUL+
  N14: Part1.D37, Axis_1_Driver.DIR+
  N15: Part1.N$21, X2.4
  N16: Part1.N$22, X2.1
  N17: Part1.3#389, X2.2
  N18: Part1.4#390, X2.3
  N19: Part1.3#393, VCC1.+, Axis_3_Driver.VCC
  N20: Part1.1, X2.8
  N21: Part1.N$29, X2.5
  N22: Part1.N$30, X2.6
  N23: Part1.4#404, X2.7
  N24: X2.14, Axis_3_Driver.A+
  N25: X2.15, Axis_3_Driver.A-
  N26: X2.16, Axis_3_Driver.B+
  N27: X2.17, Axis_3_Driver.B-
  N28: X2.18, Axis_2_Driver.A+
  N29: X2.19, Axis_2_Driver.A-
  N30: X2.20, Axis_2_Driver.B+
  N31: X2.21, Axis_2_Driver.B-
  N32: X2.22, Axis_1_Driver.A+
  N33: X2.23, Axis_1_Driver.A-
  N34: X2.24, Axis_1_Driver.B+
  N35: X2.25, Axis_1_Driver.B-
  N36: Axis_1_Driver.EN+, Axis_2_Driver.EN+, Axis_3_Driver.EN+
  N37: VCC1.-, Axis_3_Driver.GND
  N38: Axis_2_Driver.EN-, Axis_2_Driver.DIR-
  N39: Axis_3_Driver.EN-, Axis_3_Driver.DIR-

notes:
  CS-D49,
  CE-D53,
  SCK-D52
  MOSI-51
  MISO-50
  Power Feed to Sensor Control Board

custom parts:
  SIP - 13 pins: A SIP stand-in part for whatever you want. With 13 pins on a 300 mil single inline package (SIP) footprint.
