# Fritzing sketch SSPP2021-CNC_Shield_Motor_Control (saved by Fritzing 0.9.3b)

parts:
  Part1 = Arduino Uno (Rev3)
  Part2 = NRF24L01+ Breakout Board
  Axis_1 = Keyes Hall Effect Sensor [package=THT]
  KY-2 = Keyes Hall Effect Sensor [package=THT]
  KY-3 = Keyes Hall Effect Sensor [package=THT]
  KY-4 = Keyes Hall Effect Sensor [package=THT]
  KY-5 = Keyes Hall Effect Sensor [package=THT]
  Axis_6 = Keyes Hall Effect Sensor [package=THT]
  M1 = DC Motor
  L298N1 = L298N DC motor driver
  VCC1 = Battery block 9V

nets:
  N1: Part1.A5/SCL, L298N1.ENA
  N2: Part1.D8, L298N1.IN2
  N3: Part1.D9_PWM, Part2.CE
  N4: Part1.D10_PWM/SS, Part2.CS
  N5: Part1.D11_PWM/MOSI, Part2.MOSI
  N6: Part1.D12/MISO, Part2.MISO
  N7: Part1.D13/SCK, Part2.SCK
  N8: Part1.D1/TX, Axis_1.signal
  N9: Part1.D2, KY-2.signal
  N10: Part1.D3_PWM, KY-3.signal
  N11: Part1.D4, KY-4.signal
  N12: Part1.D5_PWM, KY-5.signal
  N13: Part1.D6_PWM, Axis_6.signal
  N14: Part1.D7, L298N1.IN1
  N15: Part1.5V, Axis_6.power
  N16: Part1.GND, Axis_6.ground
  N17: M1.pin_1, L298N1.OUT2
  N18: M1.pin_2, L298N1.OUT1
  N19: L298N1.12V, VCC1.+
  N20: L298N1.GND, VCC1.-

notes:
  SSPP2021 Sensor Control

custom parts:
  Keyes Hall Effect Sensor: Keyes Magnetic Hall Effect Sensor Module for Arduino. Working voltage: 4.5V-25V.
  L298N DC motor driver: 2x DC motor driver with 78M05 positive voltage regulator (7..35 V) L298N: max 46 V, 2 A Set 5 V Enable jumper to enable 5 V regultor (needed for the L298N) and +5 V output at screw terminal or supply external +5 V at screw terminal Set ENA and/or ENB to +5 V to enable motor permanently or supply ENA and/or ENB with PWM signal IN1 and IN2 set rotation directory for motor A (OUT1/OUT2) IN2 and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

// code stored in the sketch: SensorConrol.ino

